# Fritzing sketch RemoteControl (saved by Fritzing 0.9.5d)
breadboards: 1

parts:
  Компонент1 = Arduino Nano (Rev3.0)
  U1 = Sharp PC817 [package=THT]
  U2 = Sharp PC817 [package=THT]
  U3 = Sharp PC817 [package=THT]
  U4 = Sharp PC817 [package=THT]
  R1 = Resistor [tolerance=±5% resistance=220 package=THT]
  R2 = Resistor [tolerance=±5% resistance=220 package=THT]
  R3 = Resistor [tolerance=±5% resistance=220 package=THT]
  R4 = Resistor [tolerance=±5% resistance=220 package=THT]
  Main_Selector = Rotary Encoder [package=THT]
  Confirm_Key_(Menu) = Pushbutton [package="[THT]"]
  Exit/ABCD = Pushbutton [package="[THT]"]

nets:
  GND: Компонент1.GND, U1.Pin_2, U2.Pin_2, U3.Pin_2, U4.Pin_2
  N1: Компонент1.D6, R4.Pin_1
  N2: Компонент1.D8, R3.Pin_1
  N3: Компонент1.D10, R2.Pin_1
  N4: Компонент1.D12/MISO, R1.Pin_1
  N5: U1.Pin_1, R1.Pin_0
  N6: U1.Pin_4, Main_Selector.EncoderPinB
  N7: U1.Pin_3, U2.Pin_3, Main_Selector.EncoderPinC
  N8: U2.Pin_1, R2.Pin_0
  N9: U2.Pin_4, Main_Selector.EncoderPinA
  N10: U3.Pin_1, R3.Pin_0
  N11: U3.Pin_4, Confirm_Key_(Menu).Pin_3, Confirm_Key_(Menu).Pin_4
  N12: U3.Pin_3, Confirm_Key_(Menu).Pin_1, Confirm_Key_(Menu).Pin_2
  N13: U4.Pin_1, R4.Pin_0
  N14: U4.Pin_4, Exit/ABCD.Pin_3, Exit/ABCD.Pin_4
  N15: U4.Pin_3, Exit/ABCD.Pin_1, Exit/ABCD.Pin_2
